# Fritzing sketch arduino-industrial-fan-status-monitor (saved by Fritzing 1.0.7)

parts:
  M1 = 1 chan 5v relay module
  Part1 = Arduino Uno (Rev3)
  HC-SR04_Sensor_1 = HC-SR04 Ultrasonic Distance Sensor
  A1 = LED indicator 22mm

nets:
  N1: M1.pin_1, Part1.5V
  N2: M1.pin_2, Part1.GND
  N3: M1.pin_3, Part1.D13/SCK
  N4: M1.pin_4, A1.Pin_1
  N5: Part1.D5_PWM, HC-SR04_Sensor_1.TRIG
  N6: Part1.D6_PWM, HC-SR04_Sensor_1.ECHO

notes:
  24v in
  24v out
  24v gnd

custom parts:
  1 chan 5v relay module: 1 Channel 5V Relay Module Board Shield with Optocoupler Support High and Low Level Trigger for Arduino.
  LED indicator 22mm: AD16-22DS Indicator LED Power Light 22mm.
